// Digital circuit addr_decoder.dig as structural Verilog
module addr_decoder (
  input  nMREQ,
  input  A15,
  input  IOnEN,
  input  A0,
  output RAMnEN___8000__FFFF,
  output ROMnEN___0000__7FFF,
  output INnEN,
  output OUTnEN
);

  wire nand_1_out, nand_2_out, nand_3_out, nand_4_out;

  nand nand_1 (nand_1_out, nMREQ, nMREQ);
  nand nand_2 (nand_2_out, A15, A15);
  nand nand_3 (nand_3_out, IOnEN, IOnEN);
  nand nand_4 (nand_4_out, A0, A0);
  nand nand_5 (RAMnEN___8000__FFFF, nand_1_out, A15);
  nand nand_6 (ROMnEN___0000__7FFF, nand_1_out, nand_2_out);
  nand nand_7 (INnEN, nand_3_out, nand_4_out);
  nand nand_8 (OUTnEN, A0, nand_3_out);

  // Notes on the sheet:
  //   nMREQ: default 1
  //   IOnEN: default 1
endmodule
