// Digital circuit input.dig as structural Verilog
module \input  (
  input  in_1,
  input  in_2,
  input  in_3,
  input  in_4,
  input  in_5,
  input  in_6,
  input  in_7,
  input  in_8,
  input  OUTnEN,
  input  nRES,
  input  INnEN,
  input  in_20,
  input  in_21,
  input  in_22,
  input  in_23,
  input  in_24,
  input  in_25,
  input  in_26,
  input  in_27,
  output out_11,
  output out_12,
  output out_13,
  output out_14,
  output out_15,
  output out_16,
  output out_17,
  output out_18,
  output out_28,
  output out_29,
  output out_30,
  output out_31,
  output out_32,
  output out_33,
  output out_34,
  output out_35
);

  // _74273 _74273_1: pin names not known; wires that end beside it: OUTnEN, nRES, in_1, in_2, in_3, in_4, in_5, in_6, in_7, in_8, 1'b1, 1'b0, out_11, out_12, out_13, out_14, out_15, out_16, out_17, out_18
  // _74244 _74244_1: pin names not known; wires that end beside it: in_20, in_21, in_22, in_23, INnEN, in_24, in_25, in_26, in_27, INnEN, 1'b1, 1'b0, out_28, out_29, out_30, out_31, out_32, out_33, out_34, out_35

  // Notes on the sheet:
  //   OUTnEN: default 1
  //   nRES: default 1
  //   INnEN: default 1
  //   in_20: default 1
  //   in_21: default 1
  //   in_22: default 1
  //   in_23: default 1
  //   in_24: default 1
  //   in_25: default 1
  //   in_26: default 1
  //   in_27: default 1
endmodule
