// Digital circuit io.dig as structural Verilog
module io (
  input  in_1,
  input  in_2,
  input  in_3,
  input  in_4,
  input  in_5,
  input  in_6,
  input  in_7,
  input  in_8,
  input  nIORQ,
  input  nRES,
  output out_11,
  output out_12,
  output out_13,
  output out_14,
  output out_15,
  output out_16,
  output out_17,
  output out_18
);

  // _74273 _74273_1: pin names not known; wires that end beside it: nIORQ, nRES, in_1, in_2, in_3, in_4, in_5, in_6, in_7, in_8, 1'b1, 1'b0, out_11, out_12, out_13, out_14, out_15, out_16, out_17, out_18

  // Notes on the sheet:
  //   nIORQ: default 1
  //   nRES: default 1
endmodule
